// Logisim project calculadora-4bit.circ as structural Verilog: 3 circuits, main circuit main
module main (
  input  a,
  input  b,
  input  c,
  input  d,
  output x,
  output y,
  output z,
  output u,
  output v,
  output w,
  output s
);

  wire and_1_out, and_2_out, and_3_out, and_4_out, and_5_out, and_6_out, and_7_out, and_8_out, and_9_out,
       and_10_out, and_11_out, and_12_out, and_13_out, and_14_out, and_15_out, and_16_out, and_17_out,
       and_18_out, and_19_out, and_20_out, and_21_out, and_22_out, and_23_out, and_24_out, and_25_out,
       and_26_out, and_27_out, and_28_out, and_29_out, and_30_out, and_31_out, and_32_out, and_33_out,
       and_34_out, and_35_out, not_1_out, not_2_out, not_3_out, not_4_out, not_5_out, not_6_out, not_7_out,
       not_8_out, not_9_out, not_10_out, not_11_out, not_12_out, not_13_out, not_14_out, not_15_out,
       not_16_out, not_17_out, not_18_out, not_19_out, not_20_out, not_21_out, not_22_out, not_23_out,
       not_24_out, not_25_out, not_26_out, not_27_out, not_28_out, not_29_out, not_30_out, not_31_out,
       not_32_out, not_33_out, not_34_out, not_35_out, not_36_out, not_37_out, not_38_out, not_39_out,
       not_40_out, not_41_out, not_42_out, not_43_out;

  not not_1 (not_1_out, b);
  and and_1 (and_1_out, not_1_out, not_2_out);
  not not_2 (not_2_out, d);
  not not_3 (not_3_out, a);
  and and_2 (and_2_out, not_3_out, c);
  not not_4 (not_4_out, a);
  and and_3 (and_3_out, not_4_out, b, d);
  and and_4 (and_4_out, b, c);
  not not_5 (not_5_out, b);
  and and_5 (and_5_out, a, not_5_out, not_6_out);
  not not_6 (not_6_out, c);
  and and_6 (and_6_out, a, not_7_out);
  not not_7 (not_7_out, d);
  not not_8 (not_8_out, a);
  and and_7 (and_7_out, not_8_out, not_9_out);
  not not_9 (not_9_out, b);
  not not_10 (not_10_out, a);
  and and_8 (and_8_out, not_10_out, not_11_out, not_12_out);
  not not_11 (not_11_out, c);
  not not_12 (not_12_out, d);
  not not_13 (not_13_out, b);
  and and_9 (and_9_out, not_13_out, not_14_out);
  not not_14 (not_14_out, d);
  not not_15 (not_15_out, a);
  and and_10 (and_10_out, not_15_out, c, d);
  and and_11 (and_11_out, a, not_16_out, d);
  not not_16 (not_16_out, c);
  not not_17 (not_17_out, a);
  and and_12 (and_12_out, not_17_out, not_18_out);
  not not_18 (not_18_out, c);
  not not_19 (not_19_out, a);
  and and_13 (and_13_out, not_19_out, d);
  not not_20 (not_20_out, c);
  and and_14 (and_14_out, not_20_out, d);
  not not_21 (not_21_out, a);
  and and_15 (and_15_out, not_21_out, b);
  and and_16 (and_16_out, a, not_22_out);
  not not_22 (not_22_out, b);
  not not_23 (not_23_out, a);
  and and_17 (and_17_out, not_23_out, not_24_out, not_25_out);
  not not_24 (not_24_out, b);
  not not_25 (not_25_out, d);
  not not_26 (not_26_out, b);
  and and_18 (and_18_out, not_26_out, c, d);
  and and_19 (and_19_out, b, not_27_out, d);
  not not_27 (not_27_out, c);
  and and_20 (and_20_out, b, c, not_28_out);
  not not_28 (not_28_out, d);
  and and_21 (and_21_out, a, not_29_out);
  not not_29 (not_29_out, c);
  not not_30 (not_30_out, b);
  and and_22 (and_22_out, not_30_out, not_31_out);
  not not_31 (not_31_out, d);
  and and_23 (and_23_out, c, not_32_out);
  not not_32 (not_32_out, d);
  and and_24 (and_24_out, a, c);
  and and_25 (and_25_out, a, b);
  not not_33 (not_33_out, c);
  and and_26 (and_26_out, not_33_out, not_34_out);
  not not_34 (not_34_out, d);
  not not_35 (not_35_out, a);
  and and_27 (and_27_out, not_35_out, b, not_36_out);
  not not_36 (not_36_out, c);
  and and_28 (and_28_out, b, not_37_out);
  not not_37 (not_37_out, d);
  and and_29 (and_29_out, a, not_38_out);
  not not_38 (not_38_out, b);
  and and_30 (and_30_out, a, c);
  not not_39 (not_39_out, b);
  and and_31 (and_31_out, not_39_out, c);
  and and_32 (and_32_out, c, not_40_out);
  not not_40 (not_40_out, d);
  not not_41 (not_41_out, a);
  and and_33 (and_33_out, not_41_out, b, not_42_out);
  not not_42 (not_42_out, c);
  and and_34 (and_34_out, a, not_43_out);
  not not_43 (not_43_out, b);
  and and_35 (and_35_out, a, d);
  or or_1 (y, and_7_out, and_8_out, and_9_out, and_10_out, and_11_out);
  or or_2 (z, and_12_out, and_13_out, and_14_out, and_15_out, and_16_out);
  or or_3 (u, and_17_out, and_18_out, and_19_out, and_20_out, and_21_out);
  or or_4 (v, and_22_out, and_23_out, and_24_out, and_25_out);
  or or_5 (w, and_26_out, and_27_out, and_28_out, and_29_out, and_30_out);
  or or_6 (s, and_31_out, and_32_out, and_33_out, and_34_out, and_35_out);
  or or_7 (x, and_1_out, and_2_out, and_3_out, and_4_out, and_5_out, and_6_out);
endmodule

module calculadora (
  input  in_1,
  input  in_2,
  input  in_3,
  input  carry_in,
  input  in_5,
  input  in_6,
  input  in_7,
  input  in_8,
  input  in_9,
  output carry_out,
  output overflow
);

  wire main_1_s, main_1_u, main_1_v, main_1_w, main_1_x, main_1_y, main_1_z, main_2_s, main_2_u, main_2_v,
       main_2_w, main_2_x, main_2_y, main_2_z, main_3_s, main_3_u, main_3_v, main_3_w, main_3_x, main_3_y,
       main_3_z, somador_1_out_10, somador_1_out_11, somador_1_out_12, somador_1_out_13;

  main main_1 (
    .a(in_1), .b(in_2), .c(in_3), .d(in_5), .x(main_1_x), .y(main_1_y), .z(main_1_z), .u(main_1_u),
    .v(main_1_v), .w(main_1_w), .s(main_1_s));
  main main_2 (
    .a(in_6), .b(in_7), .c(in_8), .d(in_9), .x(main_2_x), .y(main_2_y), .z(main_2_z), .u(main_2_u),
    .v(main_2_v), .w(main_2_w), .s(main_2_s));
  _7_Segment_Display u_7_segment_display_1 (
    .g(main_1_s), .f(main_1_w), .a(main_1_x), .b(main_1_y), .e(main_1_v), .d(main_1_u), .c(main_1_z));  // open: dp
  _7_Segment_Display u_7_segment_display_2 (
    .g(main_2_s), .f(main_2_w), .a(main_2_x), .b(main_2_y), .e(main_2_v), .d(main_2_u), .c(main_2_z));  // open: dp
  somador somador_1 (
    .in_1(in_5), .in_2(in_3), .in_3(in_9), .in_4(in_8), .in_5(carry_in), .in_6(in_2), .in_7(in_1),
    .in_8(in_7), .in_9(in_6), .out_10(somador_1_out_10), .out_11(somador_1_out_11),
    .out_12(somador_1_out_12), .out_13(somador_1_out_13), .out_14(carry_out), .out_15(overflow));
  main main_3 (
    .a(somador_1_out_13), .b(somador_1_out_12), .c(somador_1_out_11), .d(somador_1_out_10), .x(main_3_x),
    .y(main_3_y), .z(main_3_z), .u(main_3_u), .v(main_3_v), .w(main_3_w), .s(main_3_s));
  _7_Segment_Display u_7_segment_display_3 (
    .g(main_3_s), .f(main_3_w), .a(main_3_x), .b(main_3_y), .e(main_3_v), .d(main_3_u), .c(main_3_z));  // open: dp
endmodule

module somador (
  input  in_1,
  input  in_2,
  input  in_3,
  input  in_4,
  input  in_5,
  input  in_6,
  input  in_7,
  input  in_8,
  input  in_9,
  output out_10,
  output out_11,
  output out_12,
  output out_13,
  output out_14,
  output out_15
);

  wire and_1_out, and_2_out, and_3_out, and_4_out, and_5_out, and_6_out, and_7_out, and_8_out, or_1_out,
       or_2_out, or_3_out, xor_1_out, xor_2_out, xor_5_out, xor_6_out;

  xor xor_1 (xor_1_out, in_1, in_3);
  and and_1 (and_1_out, in_1, in_3);
  xor xor_2 (xor_2_out, in_6, in_8);
  and and_2 (and_2_out, in_6, in_8);
  xor xor_3 (out_10, xor_1_out, in_5);
  and and_3 (and_3_out, xor_1_out, in_5);
  xor xor_4 (out_12, xor_2_out, or_3_out);
  and and_4 (and_4_out, xor_2_out, or_3_out);
  or or_1 (or_1_out, and_3_out, and_1_out);
  or or_2 (or_2_out, and_4_out, and_2_out);
  xor xor_5 (xor_5_out, in_2, in_4);
  and and_5 (and_5_out, in_2, in_4);
  xor xor_6 (xor_6_out, in_7, in_9);
  and and_6 (and_6_out, in_7, in_9);
  xor xor_7 (out_11, xor_5_out, or_1_out);
  and and_7 (and_7_out, xor_5_out, or_1_out);
  xor xor_8 (out_13, xor_6_out, or_2_out);
  and and_8 (and_8_out, xor_6_out, or_2_out);
  or or_3 (or_3_out, and_7_out, and_5_out);
  or or_4 (out_14, and_8_out, and_6_out);
  xor xor_9 (out_15, out_14, or_2_out);
endmodule
